# Fritzing sketch circuit_diagram (saved by Fritzing 0.9.2b)
breadboards: 2

parts:
  U1 = NodeMCU V1.0
  Squix1 = OLED 0.96" 128x64 I2C SSD1306  # not connected
  part = Resistor [tolerance=±5% resistance=1k package=THT]
  J1 = Piezo Speaker
  Right = Round Pushbutton
  Left = Round Pushbutton
  Admin_Mode = Round Pushbutton

nets:
  N1: U1.D5, Right.leg0
  N2: U1.D6, Left.leg0
  N3: part.Pin_0, J1.pin2
  N4: J1.pin1, Admin_Mode.leg1
  N5: Right.leg1, Left.leg1

custom parts:
  NodeMCU V1.0: ESP9266 based NodeMCU
